# Fritzing sketch Tetris (saved by Fritzing 0.9.3b)

parts:
  R6 = Resistor [tolerance=±5% resistance=10k package="2512 [SMD]"]
  S1_"Left" = Pushbutton [package="[THT]"]
  S2_"Down" = Pushbutton [package="[THT]"]
  S3_"Up" = Pushbutton [package="[THT]"]
  S4_"Right" = Pushbutton [package="[THT]"]
  R7 = Resistor [tolerance=±5% resistance=10k package="2512 [SMD]"]
  R8 = Resistor [tolerance=±5% resistance=10k package="2512 [SMD]"]
  R10 = Resistor [tolerance=±5% resistance=10k package="2512 [SMD]"]
  R11 = Resistor [tolerance=±5% resistance=100 package="2512 [SMD]"]
  Bauteil2 = Arduino Nano (Rev3.0) (ICSP)
  Bauteil4 = InvenSense MPU6050
  J1 = Piezo Speaker
  S6_"Mute" = Toggle Switch [package=THT]
  S7_"Joystick/Motion" = Toggle Switch [package=THT]
  LCD_display = JeePlug experimenter's board

nets:
  N1: R6.Pin_0, S4_"Right".Pin_3, S4_"Right".Pin_4, Bauteil2.D7
  GND: R6.Pin_1, R7.Pin_1, R8.Pin_1, R10.Pin_1, Bauteil2.GND, Bauteil4.GND, J1.pin1, S7_"Joystick/Motion".L2, LCD_display.A6
  N2: S1_"Left".Pin_1, S1_"Left".Pin_2, S2_"Down".Pin_1, S2_"Down".Pin_2, S3_"Up".Pin_1, S3_"Up".Pin_2, S4_"Right".Pin_1, S4_"Right".Pin_2, Bauteil2.5V, S7_"Joystick/Motion".L1
  N3: S1_"Left".Pin_3, S1_"Left".Pin_4, R7.Pin_0, Bauteil2.D6
  N4: S2_"Down".Pin_3, S2_"Down".Pin_4, R8.Pin_0, Bauteil2.D5
  N5: S3_"Up".Pin_3, S3_"Up".Pin_4, R10.Pin_0, Bauteil2.D4
  N6: R11.Pin_0, Bauteil2.D3
  N7: R11.Pin_1, S6_"Mute".COM
  N8: Bauteil2.D2, S7_"Joystick/Motion".COM
  N9: Bauteil2.D8, LCD_display.A4
  N10: Bauteil2.D9, LCD_display.A3
  N11: Bauteil2.D10, LCD_display.A5
  N12: Bauteil2.D11/MOSI, LCD_display.A2
  N13: Bauteil2.A5, Bauteil4.SCL
  N14: Bauteil2.A4, Bauteil4.SDA
  3V3: Bauteil2.3V3, Bauteil4.VCC, LCD_display.N$24, LCD_display.N$26
  N15: Bauteil2.D13/SCK, LCD_display.A1
  N16: J1.pin2, S6_"Mute".L2

notes:
  LCD display pins (left to right):
  #1: LED
  #2: SCK
  #3: SDA
  #4: AO/LOAD
  #5: RESET
  #6: CS
  #7: GND
  #8: VCC
